// Logisim project ALU.circ as structural Verilog: 1 circuit, main circuit main
module main (
  input  [7:0] in_1,
  input  [3:0] op,
  input  Zout,
  input  [7:0] b,
  output [7:0] out_5,
  output out_6,
  output out_7
);

  wire clock_1_out;
  wire [5:4] rom_2_data;
  wire [14:8] rom_1_data;

  ROM #(.addrWidth(14), .dataWidth(6)) rom_1 (
    .addr({op, b[4], out_6, b[3:0], in_1[3:0]}), .data({rom_1_data[14], rom_1_data[8], out_5[3:0]}));
  ROM #(.addrWidth(15), .dataWidth(6)) rom_2 (
    .addr({rom_1_data[14], op, out_6, rom_1_data[8], b[7:4], in_1[7:4]}), .data({rom_2_data, out_5[7:4]}));
  Clock clock_1 (.out(clock_1_out));
  D_Flip_Flop d_ff_1 (.D(rom_2_data[4]), .clk(clock_1_out), .Q(out_6), .reset(Zout));  // open: Qn, preset
  D_Flip_Flop d_ff_2 (.D(rom_2_data[5]), .clk(clock_1_out), .Q(out_7), .reset(Zout));  // open: Qn, preset

  // Notes on the sheet:
  //   a
  //   contents of rom_1 (hex, n*v repeats v):
  //   20 1 2 3 4 5 6 7 8 9 a b c d e f 1 2 3 4 5 6 7 8 9 a b c d e f 30 2 3 4 5 6 7 8 9 a b c d e f 30 11
  //   3 4 5 6 7 8 9 a b c d e f 30 11 12 4 5 6 7 8 9 a b c d e f 30 11 12 13 5 6 7 8 9 a b c d e f 30 11
  //   12 13 14 6 7 8 9 a b c d e f 30 11 12 13 14 15 7 8 9 a b c d e f 30 11 12 13 14 15 16 8 9 a b c d e
  //   f 30 11 12 13 14 15 16 17 9 a b c d e f 30 11 12 13 14 15 16 17 18 a b c d e f 30 11 12 13 14 15 16
  //   17 18 19 b c d e f 30 11 12 13 14 15 16 17 18 19 1a c d e f 30 11 12 13 14 15 16 17 18 19 1a 1b d e
  //   f 30 11 12 13 14 15 16 17 18 19 1a 1b 1c e f 30 11 12 13 14 15 16 17 18 19 1a 1b 1c 1d f 30 11 12 13
  //   14 15 16 17 18 19 1a 1b 1c 1d 1e 20 1 2 3 4 5 6 7 8 9 a b c d e f 1 2 3 4 5 6 7 8 9 a b c d e f 30 2
  //   3 4 5 6 7 8 9 a b c d e f 30 11 3 4 5 6 7 8 9 a b c d e f 30 11 12 4 5 6 7 8 9 a b c d e f 30 11 12
  //   13 5 6 7 8 9 a b c d e f 30 11 12 13 14 6 7 8 9 a b c d e f 30 11 12 13 14 15 7 8 9 a b c d e f 30
  //   11 12 13 14 15 16 8 9 a b c d e f 30 11 12 13 14 15 16 17 9 a b c d e f 30 11 12 13 14 15 16 17 18 a
  //   b c d e f 30 11 12 13 14 15 16 17 18 19 b c d e f 30 11 12 13 14 15 16 17 18 19 1a c d e f 30 11 12
  //   13 14 15 16 17 18 19 1a 1b d e f 30 11 12 13 14 15 16 17 18 19 1a 1b 1c e f 30 11 12 13 14 15 16 17
  //   18 19 1a 1b 1c 1d f 30 11 12 13 14 15 16 17 18 19 1a 1b 1c 1d 1e 20 1 2 3 4 5 6 7 8 9 a b c d e f 1
  //   2 3 4 5 6 7 8 9 a b c d e f 30 2 3 4 5 6 7 8 9 a b c d e f 30 11 3 4 5 6 7 8 9 a b c d e f 30 11 12
  //   4 5 6 7 8 9 a b c d e f 30 11 12 13 5 6 7 8 9 a b c d e f 30 11 12 13 14 6 7 8 9 a b c d e f 30 11
  //   12 13 14 15 7 8 9 a b c d e f 30 11 12 13 14 15 16 8 9 a b c d e f 30 11 12 13 14 15 16 17 9 a b c d
  //   e f 30 11 12 13 14 15 16 17 18 a b c d e f 30 11 12 13 14 15 16 17 18 19 b c d e f 30 11 12 13 14 15
  //   16 17 18 19 1a c d e f 30 11 12 13 14 15 16 17 18 19 1a 1b d e f 30 11 12 13 14 15 16 17 18 19 1a 1b
  //   1c e f 30 11 12 13 14 15 16 17 18 19 1a 1b 1c 1d f 30 11 12 13 14 15 16 17 18 19 1a 1b 1c 1d 1e 20 1
  //   2 3 4 5 6 7 8 9 a b c d e f 1 2 3 4 5 6 7 8 9 a b c d e f 30 2 3 4 5 6 7 8 9 a b c d e f 30 11 3 4 5
  //   6 7 8 9 a b c d e f 30 11 12 4 5 6 7 8 9 a b c d e f 30 11 12 13 5 6 7 8 9 a b c d e f 30 11 12 13
  //   14 6 7 8 9 a b c d e f 30 11 12 13 14 15 7 8 9 a b c d e f 30 11 12 13 14 15 16 8 9 a b c d e f 30
  //   11 12 13 14 15 16 17 9 a b c d e f 30 11 12 13 14 15 16 17 18 a b c d e f 30 11 12 13 14 15 16 17 18
  //   19 b c d e f 30 11 12 13 14 15 16 17 18 19 1a c d e f 30 11 12 13 14 15 16 17 18 19 1a 1b d e f 30
  //   11 12 13 14 15 16 17 18 19 1a 1b 1c e f 30 11 12 13 14 15 16 17 18 19 1a 1b 1c 1d f 30 11 12 13 14
  //   15 16 17 18 19 1a 1b 1c 1d 1e 20 1 2 3 4 5 6 7 8 9 a b c d e f 1f 20 1 2 3 4 5 6 7 8 9 a b c d e 1e
  //   1f 20 1 2 3 4 5 6 7 8 9 a b c d 1d 1e 1f 20 1 2 3 4 5 6 7 8 9 a b c 1c 1d 1e 1f 20 1 2 3 4 5 6 7 8 9
  //   a b 1b 1c 1d 1e 1f 20 1 2 3 4 5 6 7 8 9 a 1a 1b 1c 1d 1e 1f 20 1 2 3 4 5 6 7 8 9 19 1a 1b 1c 1d 1e
  //   1f 20 1 2 3 4 5 6 7 8 18 19 1a 1b 1c 1d 1e 1f 20 1 2 3 4 5 6 7 17 18 19 1a 1b 1c 1d 1e 1f 20 1 2 3 4
  //   5 6 16 17 18 19 1a 1b 1c 1d 1e 1f 20 1 2 3 4 5 15 16 17 18 19 1a 1b 1c 1d 1e 1f 20 1 2 3 4 14 15 16
  //   17 18 19 1a 1b 1c 1d 1e 1f 20 1 2 3 13 14 15 16 17 18 19 1a 1b 1c 1d 1e 1f 20 1 2 12 13 14 15 16 17
  //   18 19 1a 1b 1c 1d 1e 1f 20 1 11 12 13 14 15 16 17 18 19 1a 1b 1c 1d 1e 1f 20 20 1 2 3 4 5 6 7 8 9 a
  //   b c d e f 1f 20 1 2 3 4 5 6 7 8 9 a b c d e 1e 1f 20 1 2 3 4 5 6 7 8 9 a b c d 1d 1e 1f 20 1 2 3 4 5
  //   6 7 8 9 a b c 1c 1d 1e 1f 20 1 2 3 4 5 6 7 8 9 a b 1b 1c 1d 1e 1f 20 1 2 3 4 5 6 7 8 9 a 1a 1b 1c 1d
  //   1e 1f 20 1 2 3 4 5 6 7 8 9 19 1a 1b 1c 1d 1e 1f 20 1 2 3 4 5 6 7 8 18 19 1a 1b 1c 1d 1e 1f 20 1 2 3
  //   4 5 6 7 17 18 19 1a 1b 1c 1d 1e 1f 20 1 2 3 4 5 6 16 17 18 19 1a 1b 1c 1d 1e 1f 20 1 2 3 4 5 15 16
  //   17 18 19 1a 1b 1c 1d 1e 1f 20 1 2 3 4 14 15 16 17 18 19 1a 1b 1c 1d 1e 1f 20 1 2 3 13 14 15 16 17 18
  //   19 1a 1b 1c 1d 1e 1f 20 1 2 12 13 14 15 16 17 18 19 1a 1b 1c 1d 1e 1f 20 1 11 12 13 14 15 16 17 18
  //   19 1a 1b 1c 1d 1e 1f 20 20 1 2 3 4 5 6 7 8 9 a b c d e f 1f 20 1 2 3 4 5 6 7 8 9 a b c d e 1e 1f 20
  //   1 2 3 4 5 6 7 8 9 a b c d 1d 1e 1f 20 1 2 3 4 5 6 7 8 9 a b c 1c 1d 1e 1f 20 1 2 3 4 5 6 7 8 9 a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
  //   contents of rom_2 (hex, n*v repeats v):
  //   0 1 2 3 4 5 6 7 8 9 a b c d e f 1 2 3 4 5 6 7 8 9 a b c d e f 10 2 3 4 5 6 7 8 9 a b c d e f 10 11 3
  //   4 5 6 7 8 9 a b c d e f 10 11 12 4 5 6 7 8 9 a b c d e f 10 11 12 13 5 6 7 8 9 a b c d e f 10 11 12
  //   13 14 6 7 8 9 a b c d e f 10 11 12 13 14 15 7 8 9 a b c d e f 10 11 12 13 14 15 16 8 9 a b c d e f
  //   10 11 12 13 14 15 16 17 9 a b c d e f 10 11 12 13 14 15 16 17 18 a b c d e f 10 11 12 13 14 15 16 17
  //   18 19 b c d e f 10 11 12 13 14 15 16 17 18 19 1a c d e f 10 11 12 13 14 15 16 17 18 19 1a 1b d e f
  //   10 11 12 13 14 15 16 17 18 19 1a 1b 1c e f 10 11 12 13 14 15 16 17 18 19 1a 1b 1c 1d f 10 11 12 13
  //   14 15 16 17 18 19 1a 1b 1c 1d 1e 1 2 3 4 5 6 7 8 9 a b c d e f 10 2 3 4 5 6 7 8 9 a b c d e f 10 11
  //   3 4 5 6 7 8 9 a b c d e f 10 11 12 4 5 6 7 8 9 a b c d e f 10 11 12 13 5 6 7 8 9 a b c d e f 10 11
  //   12 13 14 6 7 8 9 a b c d e f 10 11 12 13 14 15 7 8 9 a b c d e f 10 11 12 13 14 15 16 8 9 a b c d e
  //   f 10 11 12 13 14 15 16 17 9 a b c d e f 10 11 12 13 14 15 16 17 18 a b c d e f 10 11 12 13 14 15 16
  //   17 18 19 b c d e f 10 11 12 13 14 15 16 17 18 19 1a c d e f 10 11 12 13 14 15 16 17 18 19 1a 1b d e
  //   f 10 11 12 13 14 15 16 17 18 19 1a 1b 1c e f 10 11 12 13 14 15 16 17 18 19 1a 1b 1c 1d f 10 11 12 13
  //   14 15 16 17 18 19 1a 1b 1c 1d 1e 10 11 12 13 14 15 16 17 18 19 1a 1b 1c 1d 1e 1f 0 1 2 3 4 5 6 7 8 9
  //   a b c d e f 1 2 3 4 5 6 7 8 9 a b c d e f 10 2 3 4 5 6 7 8 9 a b c d e f 10 11 3 4 5 6 7 8 9 a b c d
  //   e f 10 11 12 4 5 6 7 8 9 a b c d e f 10 11 12 13 5 6 7 8 9 a b c d e f 10 11 12 13 14 6 7 8 9 a b c
  //   d e f 10 11 12 13 14 15 7 8 9 a b c d e f 10 11 12 13 14 15 16 8 9 a b c d e f 10 11 12 13 14 15 16
  //   17 9 a b c d e f 10 11 12 13 14 15 16 17 18 a b c d e f 10 11 12 13 14 15 16 17 18 19 b c d e f 10
  //   11 12 13 14 15 16 17 18 19 1a c d e f 10 11 12 13 14 15 16 17 18 19 1a 1b d e f 10 11 12 13 14 15 16
  //   17 18 19 1a 1b 1c e f 10 11 12 13 14 15 16 17 18 19 1a 1b 1c 1d f 10 11 12 13 14 15 16 17 18 19 1a
  //   1b 1c 1d 1e 1 2 3 4 5 6 7 8 9 a b c d e f 10 2 3 4 5 6 7 8 9 a b c d e f 10 11 3 4 5 6 7 8 9 a b c d
  //   e f 10 11 12 4 5 6 7 8 9 a b c d e f 10 11 12 13 5 6 7 8 9 a b c d e f 10 11 12 13 14 6 7 8 9 a b c
  //   d e f 10 11 12 13 14 15 7 8 9 a b c d e f 10 11 12 13 14 15 16 8 9 a b c d e f 10 11 12 13 14 15 16
  //   17 9 a b c d e f 10 11 12 13 14 15 16 17 18 a b c d e f 10 11 12 13 14 15 16 17 18 19 b c d e f 10
  //   11 12 13 14 15 16 17 18 19 1a c d e f 10 11 12 13 14 15 16 17 18 19 1a 1b d e f 10 11 12 13 14 15 16
  //   17 18 19 1a 1b 1c e f 10 11 12 13 14 15 16 17 18 19 1a 1b 1c 1d f 10 11 12 13 14 15 16 17 18 19 1a
  //   1b 1c 1d 1e 10 11 12 13 14 15 16 17 18 19 1a 1b 1c 1d 1e 1f 0 1 2 3 4 5 6 7 8 9 a b c d e f 1f 0 1 2
  //   3 4 5 6 7 8 9 a b c d e 1e 1f 0 1 2 3 4 5 6 7 8 9 a b c d 1d 1e 1f 0 1 2 3 4 5 6 7 8 9 a b c 1c 1d
  //   1e 1f 0 1 2 3 4 5 6 7 8 9 a b 1b 1c 1d 1e 1f 0 1 2 3 4 5 6 7 8 9 a 1a 1b 1c 1d 1e 1f 0 1 2 3 4 5 6 7
  //   8 9 19 1a 1b 1c 1d 1e 1f 0 1 2 3 4 5 6 7 8 18 19 1a 1b 1c 1d 1e 1f 0 1 2 3 4 5 6 7 17 18 19 1a 1b 1c
  //   1d 1e 1f 0 1 2 3 4 5 6 16 17 18 19 1a 1b 1c 1d 1e 1f 0 1 2 3 4 5 15 16 17 18 19 1a 1b 1c 1d 1e 1f 0
  //   1 2 3 4 14 15 16 17 18 19 1a 1b 1c 1d 1e 1f 0 1 2 3 13 14 15 16 17 18 19 1a 1b 1c 1d 1e 1f 0 1 2 12
  //   13 14 15 16 17 18 19 1a 1b 1c 1d 1e 1f 0 1 11 12 13 14 15 16 17 18 19 1a 1b 1c 1d 1e 1f 0 1f 0 1 2 3
  //   4 5 6 7 8 9 a b c d e 1e 1f 0 1 2 3 4 5 6 7 8 9 a b c d 1d 1e 1f 0 1 2 3 4 5 6 7 8 9 a b c 1c 1d 1e
  //   1f 0 1 2 3 4 5 6 7 8 9 a b 1b 1c 1d 1e 1f 0 1 2 3 4 5 6 7 8 9 a 1a 1b 1c 1d 1e 1f 0 1 2 3 4 5 6 7 8
  //   9 19 1a 1b 1c 1d 1e 1f 0 1 2 3 4 5 6 7 8 18 19 1a 1b 1c 1d 1e 1f 0 1 2 3 4 5 6 7 17 18 19 1a 1b 1c
  //   1d 1e 1f 0 1 2 3 4 5 6 16 17 18 19 1a 1b 1c 1d 1e 1f 0 1 2 3 4 5 15 16 17 18 19 1a 1b 1c 1d 1e 1f 0
  //   1 2 3 4 14 15 16 17 18 19 1a 1b 1c 1d 1e 1f 0 1 2 3 13 14 15 16 17 18 19 1a 1b 1c 1d 1e 1f 0 1 2 12
  //   13 14 15 16 17 18 19 1a 1b 1c 1d 1e 1f 0 1 11 12 13 14 15 16 17 18 19 1a 1b 1c 1d 1e 1f 0 10 11 12
  //   13 14 15 16 17 18 19 1a 1b 1c 1d 1e 1f 0 1 2 3 4 5 6 7 8 9 a b c d e f 1f 0 1 2 3 4 5 6 7 8 9 a b c
  //   d e 1e 1f 0 1 2 3 4 5 6 7 8 9 a b c d 1d 1e 1f 0 1 2 3 4 5 6 7 8 9 a b c 1c 1d 1e 1f 0 1 2 3 4 5 6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
  //   Cout
endmodule
